# Fritzing sketch Trilobot_scheme (saved by Fritzing 0.9.3b)
breadboards: 2

parts:
  Součástka1 = Arduino Mega 2560 (Rev3)
  Součástka2 = Sabertooth
  M1 = Stepper Motor - Unipolar  # not connected
  M2 = Stepper Motor - Unipolar  # not connected
  C1 = Film/Foil Capacitor [capacitance=100nF voltage=35V package="5mm [THT, pp]"]
  C2 = Film/Foil Capacitor [capacitance=100nF voltage=35V package="5mm [THT, pp]"]
  R1 = Resistor [tolerance=±5% resistance=47k package="0402 [SMD]"]
  R2 = Resistor [tolerance=±5% resistance=47k package="0402 [SMD]"]
  U1 = LCD-16X2 [package=lcd-16x2_noholes]
  LCM1602_IIC1 = LCM1602 IIC [part_number="LCM1602 IIC" chip_label="LCM1602 IIC" package="DIP (Dual Inline) [THT]"]
  HC-SR04_Sensor_1 = HC-SR04 Ultrasonic Distance Sensor
  SP1 = SPEAKER [package=pcb_mount_speaker]
  X1 = Sonar
  J1 = Infrared Proximity Sensor
  R3 = Resistor [tolerance=±5% resistance=100 package="0402 [SMD]"]

nets:
  N1: Součástka1.A0, J1.Vout
  N2: Součástka1.D21/SCL, LCM1602_IIC1.SCL, X1.SCL
  N3: Součástka1.D20/SDA, LCM1602_IIC1.SDA, X1.SDA
  VCC: Součástka1.5V, LCM1602_IIC1.VCC, HC-SR04_Sensor_1.VCC, X1.+5, J1.Vcc
  GND: Součástka1.GND, Součástka2.B-, C1.-, C2.+, LCM1602_IIC1.GND, HC-SR04_Sensor_1.GND, X1.GND, J1.GND, R3.Pin_0
  N4: Součástka1.VIN, Součástka2.B+
  N5: Součástka1.D5_PWM, SP1.-
  N6: Součástka1.D6_PWM, R1.Pin_1
  N7: Součástka1.D7_PWM, R2.Pin_1
  N8: Součástka1.D24, HC-SR04_Sensor_1.TRIG
  N9: Součástka1.D26, HC-SR04_Sensor_1.ECHO
  N10: Součástka2.S1, C2.-, R2.Pin_0
  N11: Součástka2.S2, C1.+, R1.Pin_0
  VSS: U1.VSS, LCM1602_IIC1.VSS
  VDD: U1.VDD, LCM1602_IIC1.VDD
  N12: U1.VO, LCM1602_IIC1.V0
  N13: U1.RS, LCM1602_IIC1.RS
  N14: U1.R_W, LCM1602_IIC1.RW
  N15: U1.E, LCM1602_IIC1.E
  N16: U1.DB0, LCM1602_IIC1.D0
  N17: U1.DB1, LCM1602_IIC1.D1
  N18: U1.DB2, LCM1602_IIC1.D2
  N19: U1.DB3, LCM1602_IIC1.D3
  N20: U1.DB4, LCM1602_IIC1.D4
  N21: U1.DB5, LCM1602_IIC1.D5
  N22: U1.DB6, LCM1602_IIC1.D6
  N23: U1.DB7, LCM1602_IIC1.D7
  N24: U1.A, LCM1602_IIC1.A
  N25: U1.K, LCM1602_IIC1.K
  N26: LCM1602_IIC1.LED_A, LCM1602_IIC1.LED_B
  N27: SP1.+, R3.Pin_1

notes:
  9-18 V Power supply

custom parts:
  Stepper Motor - Unipolar: A basic unipolar stepper motor
  LCM1602 IIC: I2C-Module to use a 1602 or 2004 LCD on with the wire.h libory Serial LCD Modul
  Sonar: Devantech SRF08 sonar range-finder. I2C interface. Other Devantech sonars similar
